# Fritzing sketch sketch (saved by Fritzing 0.8.5b)
circuit board: 13.2278cm x 7.11468cm

parts:
  R6 = Resistor [tolerance=±5% resistance=10k package=THT]
  SW4 = Pushbutton [package="[THT]"]
  SW6 = Pushbutton [package="[THT]"]
  SW3 = Pushbutton [package="[THT]"]
  SW2 = Pushbutton [package="[THT]"]
  SW1 = Pushbutton [package="[THT]"]
  R3 = Resistor [tolerance=±5% resistance=2.2k package=THT]
  R4 = Resistor [tolerance=±5% resistance=1k package=THT]
  C6 = Ceramic Capacitor [capacitance=100nF package="100 mil [THT, multilayer]"]
  C4 = Ceramic Capacitor [capacitance=100nF package="100 mil [THT, multilayer]"]
  C3 = Ceramic Capacitor [capacitance=100nF package="100 mil [THT, multilayer]"]
  C2 = Ceramic Capacitor [capacitance=100nF package="100 mil [THT, multilayer]"]
  C1 = Ceramic Capacitor [capacitance=100nF package="100 mil [THT, multilayer]"]
  R5 = Trimmer Potentiometer [maximum_resistance=10kΩ package=THT]
  R6_2 = Resistor [tolerance=±5% resistance=470 package=THT]
  R2 = Resistor [tolerance=±5% resistance=4.7k package=THT]
  LCD1 = LCD screen
  Parte1 = Arduino Uno (Rev3)
  SW5 = Pushbutton [package="[THT]"]
  C5 = Ceramic Capacitor [capacitance=100nF package="100 mil [THT, multilayer]"]
  R5_2 = Resistor [tolerance=±5% resistance=470 package=THT]
  R1 = Resistor [tolerance=±5% resistance=10k package=THT]

nets:
  VDD: R6.Pin_0, R5.leg1, LCD1.VDD, Parte1.5V
  N1: R6.Pin_1, SW6.Pin_1, SW6.Pin_2, R3.Pin_0, R4.Pin_0, C6.1, R2.Pin_0, Parte1.A2, R5_2.Pin_0, R1.Pin_0
  N2: SW4.Pin_1, SW4.Pin_2, R4.Pin_1, C4.1
  VSS: SW4.Pin_3, SW4.Pin_4, SW6.Pin_3, SW6.Pin_4, SW3.Pin_3, SW3.Pin_4, SW2.Pin_3, SW2.Pin_4, SW1.Pin_3, SW1.Pin_4, C6.0, C4.0, C3.0, C2.0, C1.0, R5.leg2, R6_2.Pin_0, LCD1.VSS, LCD1.R/W, LCD1.LED+, Parte1.GND, SW5.Pin_3, SW5.Pin_4
  N3: SW3.Pin_1, SW3.Pin_2, R3.Pin_1, C3.1
  N4: SW2.Pin_1, SW2.Pin_2, C2.1, R2.Pin_1
  N5: SW1.Pin_1, SW1.Pin_2, C1.1, R1.Pin_1
  N6: R5.wiper, LCD1.V0
  N7: R6_2.Pin_1, LCD1.LED-
  N8: LCD1.RS, Parte1.D8
  N9: LCD1.E, Parte1.D7
  N10: LCD1.DB4, Parte1.D6_PWM
  N11: LCD1.DB5, Parte1.D5_PWM
  N12: LCD1.DB6, Parte1.D10_PWM/SS
  N13: LCD1.DB7, Parte1.D9_PWM
  N14: SW5.Pin_1, SW5.Pin_2, C5.1, R5_2.Pin_1

notes:
  AnaButtons
  https://www.github.com/pavelmc/AnaButtons/
  Pavel CO7WT <pavelmc@gmail.com>
